// Logisim project JasmineTemp2.circ as structural Verilog: 1 circuit, main circuit main
module main (
  input  [3:0] in_1,
  input  in_2,
  input  in_3,
  input  in_4,
  input  in_5,
  input  [3:0] in_6,
  output [3:0] out_7,
  output [3:0] out_8
);

  wire and_1_out, and_2_out, d_ff_1_q, d_ff_2_q, d_ff_4_q, not_1_out, or_1_out, or_2_out;
  wire [3:0] register_1_q;

  not not_1 (not_1_out, or_1_out);
  and and_1 (and_1_out, not_1_out, in_4);
  or or_1 (or_1_out, or_2_out, d_ff_1_q);
  D_Flip_Flop d_ff_1 (.D(and_1_out), .clk(in_5), .Q(d_ff_1_q));  // open: Qn, preset, reset
  Adder #(.width(4)) adder_1 (.a(in_6), .b(register_1_q));  // open: out, cin, cout
  and and_2 (and_2_out, in_2, in_3);
  D_Flip_Flop d_ff_2 (.D(d_ff_1_q), .clk(in_5), .Q(d_ff_2_q));  // open: Qn, preset, reset
  D_Flip_Flop d_ff_3 (.D(in_1[3]), .clk(and_2_out), .Q(out_7[3]));  // open: Qn, preset, reset
  or or_2 (or_2_out, d_ff_4_q, d_ff_2_q);
  Multiplier #(.width(4)) multiplier_1 (.a(in_6), .b(register_1_q));  // open: out, cin, cout
  D_Flip_Flop d_ff_4 (.D(d_ff_2_q), .clk(in_5), .Q(d_ff_4_q));  // open: Qn, preset, reset
  Subtractor #(.width(4)) subtractor_1 (.a(in_6), .b(register_1_q));  // open: out, bin, bout
  D_Flip_Flop d_ff_5 (.D(in_1[2]), .clk(and_2_out), .Q(out_7[2]));  // open: Qn, preset, reset
  Register #(.width(4)) register_1 (.en(1'b1), .clk(in_5), .Q(register_1_q));  // open: D, clr
  D_Flip_Flop d_ff_6 (.D(in_1[1]), .clk(and_2_out), .Q(out_7[1]));  // open: Qn, preset, reset
  D_Flip_Flop d_ff_7 (.D(in_1[0]), .clk(and_2_out), .Q(out_7[0]));  // open: Qn, preset, reset
endmodule
